// Logisim project ADD3.circ as structural Verilog: 1 circuit, main circuit add3
module add3 (
  input  D,
  input  C,
  input  B,
  input  A,
  output f1,
  output f2,
  output F3,
  output f4
);

  wire A_B_D_out, A_B_star_out, AD_out, AD_star_out, B_C_CD_out, B_C_D_out, B_C_out, BC_D_star_out, BC_out,
       BCD__A_B_D_out, BCD_star_out, C_D_out, C_D_star_out, CD_out, not_1_out, not_2_out, not_3_out,
       not_4_out;

  not not_1 (not_1_out, A);
  not not_2 (not_2_out, B);
  not not_3 (not_3_out, C);
  not not_4 (not_4_out, D);
  or C_D (C_D_out, D, C);
  and AD (AD_out, A, D);
  and B_C_D (B_C_D_out, C_D_out, B);
  and C_D_star (C_D_star_out, not_3_out, not_4_out);
  and AD_star (AD_star_out, A, not_4_out);
  and BC_D_star (BC_D_star_out, C_D_star_out, B);
  and B_C (B_C_out, not_2_out, C);
  or A_B_C_D (f1, B_C_D_out, A);
  or AD_BC_D_star (f2, AD_out, BC_D_star_out);
  and CD (CD_out, C, D);
  and BC (BC_out, B, C);
  or B_C_CD (B_C_CD_out, B_C_out, CD_out);
  or AD__B_C_CD (F3, AD_star_out, B_C_CD_out);
  and BCD_star (BCD_star_out, BC_out, not_4_out);
  and A_B_star (A_B_star_out, not_1_out, not_2_out);
  and A_B_D (A_B_D_out, A_B_star_out, D);
  or BCD__A_B_D (BCD__A_B_D_out, BCD_star_out, A_B_D_out);
  or AD__BCD__A_B_D (f4, AD_star_out, BCD__A_B_D_out);
endmodule
