// Logisim project BinaryToBCD.circ as structural Verilog: 1 circuit, main circuit binary
module binary (
  input  _8,
  input  _7,
  input  _6,
  input  _5,
  input  _4,
  input  _3,
  input  _2,
  input  _1,
  output H4,
  output H3,
  output H2,
  output H1,
  output T4,
  output T3,
  output T2,
  output T1,
  output U4,
  output U3,
  output U2,
  output U1
);

  wire add3_1_f1, add3_1_f2, add3_1_f3, add3_1_f4, add3_2_f2, add3_2_f3, add3_2_f4, add3_4_f1, add3_4_f2,
       add3_4_f3, add3_4_f4, add3_5_f1, add3_5_f2, add3_5_f3, add3_5_f4, add3_6_f1, add3_6_f2, add3_6_f3,
       add3_6_f4;

  add3 add3_1 (.A(1'b0), .B(_8), .C(_7), .D(_6), .f1(add3_1_f1), .f2(add3_1_f2), .F3(add3_1_f3), .f4(add3_1_f4));
  add3 add3_2 (
    .A(1'b0), .B(add3_1_f1), .C(add3_4_f1), .D(add3_5_f1), .f1(H2), .f2(add3_2_f2), .F3(add3_2_f3),
    .f4(add3_2_f4));
  add3 add3_3 (.A(add3_2_f2), .B(add3_2_f3), .C(add3_2_f4), .D(add3_6_f1), .f1(H1), .f2(T4), .F3(T3), .f4(T2));
  add3 add3_4 (
    .A(add3_1_f2), .B(add3_1_f3), .C(add3_1_f4), .D(_5), .f1(add3_4_f1), .f2(add3_4_f2), .F3(add3_4_f3),
    .f4(add3_4_f4));
  add3 add3_5 (
    .A(add3_4_f2), .B(add3_4_f3), .C(add3_4_f4), .D(_4), .f1(add3_5_f1), .f2(add3_5_f2), .F3(add3_5_f3),
    .f4(add3_5_f4));
  add3 add3_6 (
    .A(add3_5_f2), .B(add3_5_f3), .C(add3_5_f4), .D(_3), .f1(add3_6_f1), .f2(add3_6_f2), .F3(add3_6_f3),
    .f4(add3_6_f4));
  add3 add3_7 (.A(add3_6_f2), .B(add3_6_f3), .C(add3_6_f4), .D(_2), .f1(T1), .f2(U4), .F3(U3), .f4(U2));
  // add3 add3_8: pin names not known

  assign H3 = 1'b0;
  assign H4 = 1'b0;
  assign U1 = _1;
endmodule
