// Logisim project Half Adder.circ as structural Verilog: 1 circuit, main circuit Half Adder
module Half_Adder (
  input  I1,
  input  I2,
  output S,
  output C
);

  and and_1 (C, I1, I2);
  xor xor_1 (S, I1, I2);
endmodule
