// Logisim project Integer Division.circ as structural Verilog: 5 circuits, main circuit main
module main (
  input  a0,
  input  a1,
  input  a2,
  input  a3,
  input  a4,
  input  b0,
  input  b1,
  input  b2,
  input  b3,
  input  b4,
  output Q3,
  output Q2,
  output Q0,
  output Q1
);

  wire and_1_out, and_2_out, and_3_out, and_4_out, and_5_out, and_6_out, and_7_out, and_8_out, and_9_out,
       and_10_out, and_11_out, and_12_out, and_13_out, and_14_out, and_15_out, and_16_out, comparator_1_a_b,
       comparator_1_a_b_3, comparator_2_a_b, comparator_2_a_b_3, comparator_3_a_b, comparator_3_a_b_3,
       comparator_4_a_b, comparator_4_a_b_3, not_1_out, not_2_out, or_1_out, or_2_out, or_3_out, or_4_out,
       or_5_out, or_6_out, or_7_out, or_8_out, or_9_out, or_10_out, subtractor_1_out_12, subtractor_1_s1,
       subtractor_1_s2, subtractor_2_out_12, subtractor_2_s1, subtractor_2_s2, subtractor_3_out_12,
       subtractor_3_s1, subtractor_3_s2, xor_1_out;

  comparator comparator_1 (
    .a0(1'b0), .a1(1'b0), .a2(1'b0), .a3(a3), .b0(b3), .b1(b2), .b2(b1), .b3(b0), .a_b(comparator_1_a_b),
    .a_b_3(comparator_1_a_b_3));  // open: a_b_2
  xor xor_1 (xor_1_out, a4, b4);
  LED sign_flag_Q4 (.in(xor_1_out));
  _2_1_mux u_2_1_mux_1 (.d0(1'b0), .d1(1'b1), .select(or_1_out), .out_4(Q3));
  or or_1 (or_1_out, comparator_1_a_b, comparator_1_a_b_3);
  or or_2 (or_2_out, a0, a1);
  or or_3 (or_3_out, a2, a3);
  and and_1 (and_1_out, Q3, b0);
  and and_2 (and_2_out, Q3, b1);
  and and_3 (and_3_out, Q3, b2);
  and and_4 (and_4_out, Q3, b3);
  or or_4 (or_4_out, or_2_out, or_3_out);
  subtractor subtractor_1 (
    .a3(1'b0), .a2(1'b0), .a1(1'b0), .a0(a3), .b3(and_4_out), .b2(and_3_out), .b1(and_2_out), .bo(and_1_out),
    .s2(subtractor_1_s2), .s1(subtractor_1_s1), .out_12(subtractor_1_out_12));  // open: s3
  not not_1 (not_1_out, or_4_out);
  LED result_0 (.in(not_1_out));
  comparator comparator_2 (
    .a0(subtractor_1_s2), .a1(subtractor_1_s1), .a2(subtractor_1_out_12), .a3(a2), .b0(b3), .b1(b2), .b2(b1),
    .b3(b0), .a_b(comparator_2_a_b), .a_b_3(comparator_2_a_b_3));  // open: a_b_2
  or or_5 (or_5_out, b3, b2);
  or or_6 (or_6_out, b1, b0);
  or or_7 (or_7_out, or_5_out, or_6_out);
  _2_1_mux u_2_1_mux_2 (.d0(1'b0), .d1(1'b1), .select(or_8_out), .out_4(Q2));
  or or_8 (or_8_out, comparator_2_a_b, comparator_2_a_b_3);
  not not_2 (not_2_out, or_7_out);
  LED divison_by_0 (.in(not_2_out));
  and and_5 (and_5_out, Q2, b1);
  and and_6 (and_6_out, Q2, b2);
  and and_7 (and_7_out, Q2, b3);
  and and_8 (and_8_out, Q2, b0);
  subtractor subtractor_2 (
    .a3(subtractor_1_s2), .a2(subtractor_1_s1), .a1(subtractor_1_out_12), .a0(a2), .b3(and_7_out),
    .b2(and_6_out), .b1(and_5_out), .bo(and_8_out), .s2(subtractor_2_s2), .s1(subtractor_2_s1),
    .out_12(subtractor_2_out_12));  // open: s3
  comparator comparator_3 (
    .a0(subtractor_2_s2), .a1(subtractor_2_s1), .a2(subtractor_2_out_12), .a3(a1), .b0(b3), .b1(b2), .b2(b1),
    .b3(b0), .a_b(comparator_3_a_b), .a_b_3(comparator_3_a_b_3));  // open: a_b_2
  _2_1_mux u_2_1_mux_3 (.d0(1'b0), .d1(1'b1), .select(or_9_out), .out_4(Q1));
  or or_9 (or_9_out, comparator_3_a_b, comparator_3_a_b_3);
  and and_9 (and_9_out, Q1, b0);
  and and_10 (and_10_out, Q1, b1);
  and and_11 (and_11_out, Q1, b2);
  and and_12 (and_12_out, Q1, b3);
  subtractor subtractor_3 (
    .a3(subtractor_2_s2), .a2(subtractor_2_s1), .a1(subtractor_2_out_12), .a0(a1), .b3(and_12_out),
    .b2(and_11_out), .b1(and_10_out), .bo(and_9_out), .s2(subtractor_3_s2), .s1(subtractor_3_s1),
    .out_12(subtractor_3_out_12));  // open: s3
  comparator comparator_4 (
    .a0(subtractor_3_s2), .a1(subtractor_3_s1), .a2(subtractor_3_out_12), .a3(a0), .b0(b3), .b1(b2), .b2(b1),
    .b3(b0), .a_b(comparator_4_a_b), .a_b_3(comparator_4_a_b_3));  // open: a_b_2
  or or_10 (or_10_out, comparator_4_a_b, comparator_4_a_b_3);
  _2_1_mux u_2_1_mux_4 (.d0(1'b0), .d1(1'b1), .select(or_10_out), .out_4(Q0));
  and and_13 (and_13_out, Q0, b0);
  and and_14 (and_14_out, Q0, b1);
  and and_15 (and_15_out, Q0, b2);
  and and_16 (and_16_out, Q0, b3);
  subtractor subtractor_4 (
    .a3(subtractor_3_s2), .a2(subtractor_3_s1), .a1(subtractor_3_out_12), .a0(a0), .b3(and_16_out),
    .b2(and_15_out), .b1(and_14_out), .bo(and_13_out));  // open: s3, s2, s1, out_12
endmodule

module FA (
  input  a,
  input  b,
  input  c,
  output x,
  output y
);

  wire and_1_out, and_2_out, and_3_out, and_4_out, and_5_out, and_6_out, and_7_out, not_1_out, not_2_out,
       not_3_out, not_4_out, not_5_out, not_6_out;

  not not_1 (not_1_out, a);
  not not_2 (not_2_out, b);
  not not_3 (not_3_out, a);
  not not_4 (not_4_out, c);
  not not_5 (not_5_out, b);
  not not_6 (not_6_out, c);
  and and_1 (and_1_out, b, c);
  and and_2 (and_2_out, a, c);
  and and_3 (and_3_out, a, b);
  and and_4 (and_4_out, not_1_out, not_2_out, c);
  and and_5 (and_5_out, not_3_out, b, not_4_out);
  and and_6 (and_6_out, a, not_5_out, not_6_out);
  and and_7 (and_7_out, a, b, c);
  or or_1 (y, and_1_out, and_2_out, and_3_out);
  or or_2 (x, and_4_out, and_5_out, and_6_out, and_7_out);

  // Notes on the sheet:
  //   sum
  //   carry
endmodule

module subtractor (
  input  a3,
  input  a2,
  input  a1,
  input  a0,
  input  b3,
  input  b2,
  input  b1,
  input  bo,
  output s3,
  output s2,
  output s1,
  output out_12
);

  wire fa_1_y, fa_2_y, fa_3_y, fa_4_y, not_1_out, not_2_out, not_3_out, not_4_out;

  not not_1 (not_1_out, b3);
  FA fa_1 (.a(a3), .b(not_1_out), .c(fa_2_y), .x(s3), .y(fa_1_y));
  not not_2 (not_2_out, b2);
  FA fa_2 (.a(a2), .b(not_2_out), .c(fa_3_y), .x(s2), .y(fa_2_y));
  not not_3 (not_3_out, b1);
  FA fa_3 (.a(a1), .b(not_3_out), .c(fa_4_y), .x(s1), .y(fa_3_y));
  not not_4 (not_4_out, bo);
  FA fa_4 (.a(a0), .b(not_4_out), .c(1'b1), .x(out_12), .y(fa_4_y));
endmodule

module _2_1_mux (
  input  d0,
  input  d1,
  input  select,
  output out_4
);

  wire and_1_out, and_2_out, not_1_out;

  not not_1 (not_1_out, select);
  and and_1 (and_1_out, d0, not_1_out);
  and and_2 (and_2_out, d1, select);
  or or_1 (out_4, and_1_out, and_2_out);
endmodule

module comparator (
  input  a0,
  input  a1,
  input  a2,
  input  a3,
  input  b0,
  input  b1,
  input  b2,
  input  b3,
  output a_b,
  output a_b_2,
  output a_b_3
);

  wire and_1_out, and_2_out, and_3_out, and_5_out, and_6_out, and_7_out, and_8_out, and_9_out, and_10_out,
       and_11_out, and_12_out, and_13_out, and_14_out, and_15_out, not_1_out, not_2_out, not_3_out,
       not_4_out, not_5_out, not_6_out, not_7_out, not_8_out, not_9_out, not_10_out, or_1_out, or_2_out,
       xor_1_out, xor_2_out, xor_3_out, xor_4_out;

  xor xor_1 (xor_1_out, a0, b0);
  xor xor_2 (xor_2_out, a1, b1);
  xor xor_3 (xor_3_out, a2, b2);
  xor xor_4 (xor_4_out, a3, b3);
  not not_1 (not_1_out, xor_1_out);
  not not_2 (not_2_out, xor_2_out);
  not not_3 (not_3_out, xor_3_out);
  not not_4 (not_4_out, b0);
  not not_5 (not_5_out, b1);
  not not_6 (not_6_out, b2);
  not not_7 (not_7_out, b3);
  not not_8 (not_8_out, xor_4_out);
  and and_1 (and_1_out, not_1_out, not_5_out);
  and and_2 (and_2_out, a1, a1);
  and and_3 (and_3_out, not_1_out, not_2_out);
  and and_4 (a_b, and_3_out, and_5_out);
  and and_5 (and_5_out, not_3_out, not_8_out);
  and and_6 (and_6_out, not_4_out, a0);
  and and_7 (and_7_out, and_1_out, and_2_out);
  and and_8 (and_8_out, not_2_out, not_1_out);
  and and_9 (and_9_out, a2, not_6_out);
  and and_10 (and_10_out, not_1_out, not_2_out);
  and and_11 (and_11_out, not_3_out, not_7_out);
  and and_12 (and_12_out, a3, a3);
  and and_13 (and_13_out, and_8_out, and_9_out);
  and and_14 (and_14_out, and_10_out, and_11_out);
  and and_15 (and_15_out, and_14_out, and_12_out);
  or or_1 (or_1_out, and_6_out, and_7_out);
  or or_2 (or_2_out, and_13_out, not_9_out);
  not not_9 (not_9_out, not_10_out);
  not not_10 (not_10_out, and_15_out);
  or or_3 (a_b_3, or_1_out, or_2_out);
  nor nor_1 (a_b_2, a_b, a_b_3);
endmodule
