// Logisim project MULTandBinaryToBCD.circ as structural Verilog: 5 circuits, main circuit BITOBCD
module BITOBCD (
  input  _8,
  input  _7,
  input  _6,
  input  _5,
  input  _4,
  input  _3,
  input  _2,
  input  _1,
  output H4,
  output H3,
  output H2,
  output H1,
  output T4,
  output T3,
  output T2,
  output T1,
  output U4,
  output U3,
  output U2,
  output U1
);

  wire add3_1_f1, add3_1_f2, add3_1_f3, add3_1_f4, add3_2_f2, add3_2_f3, add3_2_f4, add3_4_f1, add3_4_f2,
       add3_4_f3, add3_4_f4, add3_5_f1, add3_5_f2, add3_5_f3, add3_5_f4, add3_6_f1, add3_6_f2, add3_6_f3,
       add3_6_f4;

  ADD3 add3_1 (.D(_6), .C(_7), .B(_8), .A(1'b0), .f1(add3_1_f1), .f2(add3_1_f2), .F3(add3_1_f3), .f4(add3_1_f4));
  ADD3 add3_2 (
    .D(add3_5_f1), .C(add3_4_f1), .B(add3_1_f1), .A(1'b0), .f1(H2), .f2(add3_2_f2), .F3(add3_2_f3),
    .f4(add3_2_f4));
  ADD3 add3_3 (.D(add3_6_f1), .C(add3_2_f4), .B(add3_2_f3), .A(add3_2_f2), .f1(H1), .f2(T4), .F3(T3), .f4(T2));
  ADD3 add3_4 (
    .D(_5), .C(add3_1_f4), .B(add3_1_f3), .A(add3_1_f2), .f1(add3_4_f1), .f2(add3_4_f2), .F3(add3_4_f3),
    .f4(add3_4_f4));
  ADD3 add3_5 (
    .D(_4), .C(add3_4_f4), .B(add3_4_f3), .A(add3_4_f2), .f1(add3_5_f1), .f2(add3_5_f2), .F3(add3_5_f3),
    .f4(add3_5_f4));
  ADD3 add3_6 (
    .D(_3), .C(add3_5_f4), .B(add3_5_f3), .A(add3_5_f2), .f1(add3_6_f1), .f2(add3_6_f2), .F3(add3_6_f3),
    .f4(add3_6_f4));
  ADD3 add3_7 (.D(_2), .C(add3_6_f4), .B(add3_6_f3), .A(add3_6_f2), .f1(T1), .f2(U4), .F3(U3), .f4(U2));

  assign H3 = 1'b0;
  assign H4 = 1'b0;
  assign U1 = _1;
endmodule

module HA (
  input  I1,
  input  I2,
  output S,
  output C
);

  and and_1 (C, I1, I2);
  xor xor_1 (S, I1, I2);
endmodule

module FA (
  input  In1,
  input  In2,
  input  In3,
  output S,
  output C
);

  wire ha_1_c, ha_1_s, ha_2_c;

  HA ha_1 (.I1(In1), .I2(In2), .S(ha_1_s), .C(ha_1_c));
  HA ha_2 (.I1(ha_1_s), .I2(In3), .S(S), .C(ha_2_c));
  or or_1 (C, ha_2_c, ha_1_c);
endmodule

module MULT (
  input  B4,
  input  B3,
  input  B2,
  input  B1,
  input  B0,
  input  A0,
  input  A1,
  input  A2,
  input  A3,
  input  A4,
  output Sign,
  output L8,
  output L7,
  output L6,
  output L5,
  output L4,
  output L3,
  output L2,
  output L1,
  output Result_0
);

  wire and_1_out, and_2_out, and_3_out, and_4_out, and_5_out, and_6_out, and_7_out, and_8_out, and_9_out,
       and_10_out, and_11_out, and_12_out, and_13_out, and_14_out, and_15_out, fa_2_c, fa_2_s, fa_3_c,
       fa_4_c, fa_4_s, fa_5_c, fa_5_s, fa_6_c, fa_7_c, fa_7_s, fa_8_c, fa_8_s, fa_9_c, fa_10_c, fa_10_s,
       fa_11_c, fa_12_c, or_1_out, or_2_out, or_3_out, or_4_out, or_5_out, or_6_out, or_7_out;

  xor xor_1 (Sign, A4, B4);
  and and_1 (and_1_out, B3, A3);
  or or_1 (or_1_out, L8, L7);
  and and_2 (and_2_out, B3, A2);
  and and_3 (and_3_out, B2, A3);
  FA fa_1 (.In1(fa_3_c), .In2(fa_2_c), .In3(and_1_out), .S(L7), .C(L8));
  or or_2 (or_2_out, or_1_out, or_3_out);
  FA fa_2 (.In1(fa_5_c), .In2(fa_4_c), .In3(and_2_out), .S(fa_2_s), .C(fa_2_c));
  FA fa_3 (.In1(fa_6_c), .In2(fa_2_s), .In3(and_3_out), .S(L6), .C(fa_3_c));
  and and_4 (and_4_out, B3, A1);
  and and_5 (and_5_out, B2, A2);
  and and_6 (and_6_out, B1, A3);
  or or_3 (or_3_out, L6, L5);
  FA fa_4 (.In1(fa_7_c), .In2(1'b0), .In3(and_4_out), .S(fa_4_s), .C(fa_4_c));
  FA fa_5 (.In1(fa_8_c), .In2(fa_4_s), .In3(and_5_out), .S(fa_5_s), .C(fa_5_c));
  FA fa_6 (.In1(fa_9_c), .In2(fa_5_s), .In3(and_6_out), .S(L5), .C(fa_6_c));
  and and_7 (and_7_out, B2, A1);
  and and_8 (and_8_out, B1, A2);
  and and_9 (and_9_out, B0, A3);
  or or_4 (or_4_out, or_2_out, or_6_out);
  not not_1 (Result_0, or_4_out);
  and and_10 (and_10_out, B3, A0);
  FA fa_7 (.In1(fa_10_c), .In2(and_10_out), .In3(and_7_out), .S(fa_7_s), .C(fa_7_c));
  FA fa_8 (.In1(fa_11_c), .In2(fa_7_s), .In3(and_8_out), .S(fa_8_s), .C(fa_8_c));
  and and_11 (and_11_out, B1, A1);
  and and_12 (and_12_out, B0, A2);
  FA fa_9 (.In1(1'b0), .In2(fa_8_s), .In3(and_9_out), .S(L4), .C(fa_9_c));
  and and_13 (and_13_out, B2, A0);
  or or_5 (or_5_out, L4, L3);
  FA fa_10 (.In1(fa_12_c), .In2(and_13_out), .In3(and_11_out), .S(fa_10_s), .C(fa_10_c));
  FA fa_11 (.In1(1'b0), .In2(fa_10_s), .In3(and_12_out), .S(L3), .C(fa_11_c));
  and and_14 (and_14_out, B0, A1);
  or or_6 (or_6_out, or_5_out, or_7_out);
  and and_15 (and_15_out, B1, A0);
  FA fa_12 (.In1(1'b0), .In2(and_15_out), .In3(and_14_out), .S(L2), .C(fa_12_c));
  or or_7 (or_7_out, L2, L1);
  and and_16 (L1, B0, A0);
endmodule

module ADD3 (
  input  D,
  input  C,
  input  B,
  input  A,
  output f1,
  output f2,
  output F3,
  output f4
);

  wire A_B_D_out, A_B_star_out, AD_out, AD_star_out, B_C_CD_out, B_C_D_out, B_C_out, BC_D_star_out, BC_out,
       BCD__A_B_D_out, BCD_star_out, C_D_out, C_D_star_out, CD_out, not_1_out, not_2_out, not_3_out,
       not_4_out;

  not not_1 (not_1_out, A);
  not not_2 (not_2_out, B);
  not not_3 (not_3_out, C);
  not not_4 (not_4_out, D);
  or C_D (C_D_out, D, C);
  and AD (AD_out, A, D);
  and B_C_D (B_C_D_out, C_D_out, B);
  and C_D_star (C_D_star_out, not_3_out, not_4_out);
  and AD_star (AD_star_out, A, not_4_out);
  and BC_D_star (BC_D_star_out, C_D_star_out, B);
  and B_C (B_C_out, not_2_out, C);
  or A_B_C_D (f1, B_C_D_out, A);
  or AD_BC_D_star (f2, AD_out, BC_D_star_out);
  and CD (CD_out, C, D);
  and BC (BC_out, B, C);
  or B_C_CD (B_C_CD_out, B_C_out, CD_out);
  or AD__B_C_CD (F3, AD_star_out, B_C_CD_out);
  and BCD_star (BCD_star_out, BC_out, not_4_out);
  and A_B_star (A_B_star_out, not_1_out, not_2_out);
  and A_B_D (A_B_D_out, A_B_star_out, D);
  or BCD__A_B_D (BCD__A_B_D_out, BCD_star_out, A_B_D_out);
  or AD__BCD__A_B_D (f4, AD_star_out, BCD__A_B_D_out);
endmodule
