// Logisim project ModeOfOperation.circ as structural Verilog: 1 circuit, main circuit 4:1MUX
module _4_1MUX (
  input  I0,
  input  I1,
  input  I2,
  input  I3,
  input  S1,
  input  S0,
  output O
);

  wire and_1_out, and_2_out, and_3_out, and_4_out, and_5_out, and_6_out, and_7_out, and_8_out, not_1_out,
       not_2_out, or_1_out, or_2_out;

  not not_1 (not_1_out, S1);
  not not_2 (not_2_out, S0);
  and and_1 (and_1_out, not_1_out, not_2_out);
  and and_2 (and_2_out, not_1_out, S0);
  and and_3 (and_3_out, S1, not_2_out);
  and and_4 (and_4_out, S1, S0);
  and and_5 (and_5_out, and_1_out, I0);
  and and_6 (and_6_out, and_2_out, I1);
  and and_7 (and_7_out, and_3_out, I2);
  and and_8 (and_8_out, and_4_out, I3);
  or or_1 (or_1_out, and_5_out, and_6_out);
  or or_2 (or_2_out, and_7_out, and_8_out);
  or or_3 (O, or_1_out, or_2_out);
endmodule
